# Fritzing sketch viol1 (saved by Fritzing 1.0.8)
breadboards: 1

parts:
  Part1 = Adafruit ESP32 Feather V2
  LED1 = LED - 5mm [color="Red (633nm)" current=0.030A package="5 mm [THT]"]
  LED2 = LED - 5mm [color="Red (633nm)" current=0.030A package="5 mm [THT]"]
  R1 = Textile Analog Pressure Sensor [part_number=PW073]
  R2 = Textile Analog Pressure Sensor [part_number=PW073]
  R3 = Textile Analog Pressure Sensor [part_number=PW073]
  R4 = Resistor [tolerance=±5% power=0.25W resistance=100 package=THT]
  R5 = Resistor [tolerance=±5% power=0.25W resistance=100 package=THT]
  R6 = Resistor [tolerance=±5% power=0.25W resistance=100 package=THT]
  R7 = Resistor [tolerance=±5% power=0.25W resistance=10k package=THT]
  R8 = Resistor [tolerance=±5% power=0.25W resistance=10k package=THT]
  LED3 = LED - 5mm [color="Red (633nm)" current=0.030A package="5 mm [THT]"]

nets:
  N1: Part1.SDA, Part1.IO27_A10, R4.Pin_1
  N2: Part1.A5_IO4, R5.Pin_1
  N3: Part1.A2_I34, R1.pin_0, R8.Pin_0
  N4: Part1.A1_DAC1, R2.pin_0, R3.pin_0, R7.Pin_0
  N5: Part1.A0_DAC2, R6.Pin_1
  N6: Part1.GND, LED1.cathode, LED2.cathode, R7.Pin_1, R8.Pin_1, LED3.anode
  N7: Part1.3.3V, R1.pin_1, R2.pin_1, R3.pin_1
  N8: LED1.anode, R5.Pin_0
  N9: LED2.anode, R6.Pin_0
  N10: R4.Pin_0, LED3.cathode

notes:
  Distance pressure sensor pad 1.
  Distance pressure sensor pad 2.
  Proximity pressure sensor pad.
